// Digital circuit Calculator.dig as structural Verilog
module Calculator (
);

  wire _0, _1, _2, _3, _4, _5, _6, _7, _8, _9, a, ao, c, d, \do , e, err, m, mo, ne, s, so;
  wire [6:0] o1, o2, o3, o4, o5, o6, o7, o8, r1, r2, r3, r4;

  Seven_Seg seven_seg_1 (.a(o4[6]), .b(o4[5]), .c(o4[4]), .d(o4[3]), .e(o4[2]), .f(o4[1]), .g(o4[0]), .dp(1'b0));
  Seven_Seg seven_seg_2 (.a(o3[6]), .b(o3[5]), .c(o3[4]), .d(o3[3]), .e(o3[2]), .f(o3[1]), .g(o3[0]), .dp(1'b0));
  Seven_Seg seven_seg_3 (.a(o2[6]), .b(o2[5]), .c(o2[4]), .d(o2[3]), .e(o2[2]), .f(o2[1]), .g(o2[0]), .dp(1'b0));
  Seven_Seg seven_seg_4 (.a(o1[6]), .b(o1[5]), .c(o1[4]), .d(o1[3]), .e(o1[2]), .f(o1[1]), .g(o1[0]), .dp(1'b0));
  LED plus (.in(ao));
  LED led (.in(so));
  LED x (.in(mo));
  LED led_2 (.in(\do ));
  Button u__1 (.out(_1));
  Button u__4 (.out(_4));
  Button u__7 (.out(_7));
  Button u_C (.out(c));
  Seven_Seg seven_seg_5 (.a(o8[6]), .b(o8[5]), .c(o8[4]), .d(o8[3]), .e(o8[2]), .f(o8[1]), .g(o8[0]), .dp(1'b0));
  Button u__2 (.out(_2));
  Button u__5 (.out(_5));
  Button u__8 (.out(_8));
  Button u__0 (.out(_0));
  Button u__3 (.out(_3));
  Button u__6 (.out(_6));
  Button u__9 (.out(_9));
  Button eq (.out(e));
  Seven_Seg seven_seg_6 (.a(o7[6]), .b(o7[5]), .c(o7[4]), .d(o7[3]), .e(o7[2]), .f(o7[1]), .g(o7[0]), .dp(1'b0));
  Button plus_2 (.out(a));
  Button button (.out(s));
  Button x_2 (.out(m));
  Button button_2 (.out(d));
  Seven_Seg seven_seg_7 (.a(o6[6]), .b(o6[5]), .c(o6[4]), .d(o6[3]), .e(o6[2]), .f(o6[1]), .g(o6[0]), .dp(1'b0));
  Seven_Seg seven_seg_8 (.a(o5[6]), .b(o5[5]), .c(o5[4]), .d(o5[3]), .e(o5[2]), .f(o5[1]), .g(o5[0]), .dp(1'b0));
  LED MINUS (.in(ne));
  io_module io_module_1 (
    .num({_9, _8, _7, _6, _5, _4, _3, _2, _1, _0}), .ops({d, m, s, a}), .eq(e), .c(c), .s1(o1), .s2(o2),
    .s3(o3), .s4(o4), .s5(o5), .s6(o6), .s7(o7), .s8(o8), .a(ao), .s(so), .m(mo), .d(\do ), .err(err),
    .r1(r1), .r2(r2), .r3(r3), .r4(r4), .ne(ne));
  Seven_Seg seven_seg_9 (.a(r4[6]), .b(r4[5]), .c(r4[4]), .d(r4[3]), .e(r4[2]), .f(r4[1]), .g(r4[0]), .dp(1'b0));
  Seven_Seg seven_seg_10 (.a(r3[6]), .b(r3[5]), .c(r3[4]), .d(r3[3]), .e(r3[2]), .f(r3[1]), .g(r3[0]), .dp(1'b0));
  Seven_Seg seven_seg_11 (.a(r2[6]), .b(r2[5]), .c(r2[4]), .d(r2[3]), .e(r2[2]), .f(r2[1]), .g(r2[0]), .dp(1'b0));
  LED Error (.in(err));
  Seven_Seg seven_seg_12 (.a(r1[6]), .b(r1[5]), .c(r1[4]), .d(r1[3]), .e(r1[2]), .f(r1[1]), .g(r1[0]), .dp(1'b0));

  // Notes on the sheet:
  //   Keyboard
  //   Brain
  //   =
endmodule
