// Digital circuit Addition.dig as structural Verilog
module Addition (
  input  [15:0] B,
  input  [15:0] A,
  output err,
  output [31:0] F
);

  wire comparator_1_eq, comparator_1_lt;
  wire [0:0] or_1_out;
  wire [15:0] add_1_s;

  Add #(.Bits(16)) add_1 (.a(A), .b(B), .c_i(1'b0), .s(add_1_s));  // open: c_o
  Comparator #(.Signed("true"), .Bits(16)) comparator_1 (
    .a(add_1_s), .b(16'h270f), .gt(err), .eq(comparator_1_eq), .lt(comparator_1_lt));
  or or_1 (or_1_out[0], comparator_1_eq, comparator_1_lt);
  Mul #(.Signed("true"), .Bits(16)) mul_1 (.a(add_1_s), .b({{15{1'b0}}, or_1_out[0]}), .mul(F));

  // Notes on the sheet:
  //   Addition
  //   Test
endmodule

/* Test case:
A B F error
1 1 2 0
1000 2400 3400 0
9999 1 0 1
4000 9999 0 1
234 211 445 0
3221 6431 9652 0
0 0 0 0
1222 2111 3333 0
*/
