// Digital circuit Division.dig as structural Verilog
module Division (
  input  [15:0] B,
  input  [15:0] A,
  output [31:0] F,
  output err
);

  wire comparator_1_gt, comparator_1_lt;
  wire [0:0] or_1_out;
  wire [15:0] div_1_q;

  Div #(.Signed("true"), .Bits(16)) div_1 (.a(A), .b(B), .q(div_1_q));  // open: r
  Comparator #(.Signed("true"), .Bits(16)) comparator_1 (
    .a(B), .b({16{1'b0}}), .gt(comparator_1_gt), .eq(err), .lt(comparator_1_lt));
  or or_1 (or_1_out[0], comparator_1_gt, comparator_1_lt);
  Mul #(.Signed("true"), .Bits(16)) mul_1 (.a(div_1_q), .b({{15{1'b0}}, or_1_out[0]}), .mul(F));

  // Notes on the sheet:
  //   Division
  //   Test
endmodule

/* Test case:
A B F error
1 1 1 0
1000 2400 0 0
9999 1 9999 0
4000 2 2000 0
20 20 1 0
500 12 41 0
0 0 0 1
1222 2111 0 0
*/
