// Digital circuit Multiplication.dig as structural Verilog
module Multiplication (
  input  [15:0] B,
  input  [15:0] A,
  output err,
  output [63:0] F
);

  wire comparator_1_eq, comparator_1_lt;
  wire [0:0] or_1_out;
  wire [31:0] mul_1_mul;

  Mul #(.Signed("true"), .Bits(16)) mul_1 (.a(A), .b(B), .mul(mul_1_mul));
  Comparator #(.Signed("true"), .Bits(32)) comparator_1 (
    .a(mul_1_mul), .b(32'h270f), .gt(err), .eq(comparator_1_eq), .lt(comparator_1_lt));
  or or_1 (or_1_out[0], comparator_1_eq, comparator_1_lt);
  Mul #(.Signed("true"), .Bits(32)) mul_2 (.a(mul_1_mul), .b({{31{1'b0}}, or_1_out[0]}), .mul(F));

  // Notes on the sheet:
  //   Multiplication
  //   Test
endmodule

/* Test case:
A B F error
1 1 1 0
1000 2400 0 1
9999 1 9999 0
4000 9999 0 1
20 20 400 0
500 12 6000 0
0 0 0 0
1222 2111 0 1
*/
