// Digital circuit Subtraction.dig as structural Verilog
module Subtraction (
  input  [15:0] B,
  input  [15:0] A,
  output [15:0] F
);

  Sub #(.Bits(16)) sub_1 (.a(A), .b(B), .c_i(1'b0), .s(F));  // open: c_o

  // Notes on the sheet:
  //   Substraction
  //   Test
endmodule

/* Test case:
A B F
1 1 0
500 240 260
9999 1 9998 
3000 5000 0b1111100000110000
1 9999 0b1101100011110010
9999 1 9998
1231 121 1110
1312 1312 0
0 0 0
*/
