// Digital circuit arithmetic_module.dig as structural Verilog
module arithmetic_module (
  input  [15:0] in_a,
  input  [15:0] in_b,
  input  a,
  input  s,
  input  m,
  input  d,
  input  c,
  output [15:0] out,
  output err,
  output neg,
  output en
);

  wire addition_1_err, division_1_err, multiplication_1_err;
  wire [15:0] subtraction_1_f;
  wire [31:0] addition_1_f, division_1_f;
  wire [63:0] multiplication_1_f;

  Addition addition_1 (.B(in_b), .A(in_a), .err(addition_1_err), .F(addition_1_f));
  Subtraction subtraction_1 (.B(in_b), .A(in_a), .F(subtraction_1_f));
  Multiplication multiplication_1 (.B(in_b), .A(in_a), .err(multiplication_1_err), .F(multiplication_1_f));
  Division division_1 (.B(in_b), .A(in_a), .F(division_1_f), .err(division_1_err));
  op_selector #(.applicationType("IVERILOG"), .CodeFile("C:\\Users\\metin\\Desktop\\Project101\\verilog_codes\\op_selector.v")) u_op_selector (
    .a_in(addition_1_f), .s_in(subtraction_1_f), .m_in(multiplication_1_f), .d_in(division_1_f),
    .a_er(addition_1_err), .m_er(multiplication_1_err), .d_er(division_1_err), .a(a), .s(s), .m(m), .d(d),
    .reset(c), .enable(en), .abs_out(out), .err(err), .neg(neg));

  // Notes on the sheet:
  //   in_a: default 20
  //   in_b: default 20
endmodule
