// Digital circuit bcd_to_7s_encoder_module.dig as structural Verilog
module bcd_to_7s_encoder_module (
  input  [3:0] in,
  input  en,
  output [6:0] out
);

  wire and_1_out, and_2_out, and_4_out, and_6_out, and_8_out, and_9_out, and_11_out, and_12_out, and_13_out,
       and_15_out, and_16_out, and_17_out, and_19_out, and_20_out, and_21_out, and_23_out, not_1_out,
       not_2_out, not_3_out, not_4_out, or_1_out, or_2_out, or_3_out, or_4_out, or_5_out, or_6_out, or_7_out;

  not not_1 (not_1_out, in[3]);
  not not_2 (not_2_out, in[2]);
  not not_3 (not_3_out, in[1]);
  not not_4 (not_4_out, in[0]);
  and and_1 (and_1_out, not_4_out, not_2_out);
  and and_2 (and_2_out, in[0], in[2]);
  and and_3 (out[6], or_1_out, en);
  or or_1 (or_1_out, in[3], in[1], and_2_out, and_1_out);
  and and_4 (and_4_out, not_4_out, not_3_out);
  and and_5 (out[5], or_2_out, en);
  and and_6 (and_6_out, in[0], in[1]);
  or or_2 (or_2_out, and_6_out, not_2_out, and_4_out);
  and and_7 (out[4], or_3_out, en);
  or or_3 (or_3_out, in[2], in[0], not_3_out);
  and and_8 (and_8_out, not_4_out, not_2_out);
  and and_9 (and_9_out, in[1], not_2_out);
  and and_10 (out[3], or_4_out, en);
  and and_11 (and_11_out, not_4_out, in[1]);
  or or_4 (or_4_out, and_12_out, and_11_out, in[3], and_9_out, and_8_out);
  and and_12 (and_12_out, in[0], not_3_out, in[2]);
  and and_13 (and_13_out, not_4_out, not_2_out);
  or or_5 (or_5_out, and_15_out, and_13_out);
  and and_14 (out[2], or_5_out, en);
  and and_15 (and_15_out, not_4_out, in[1]);
  and and_16 (and_16_out, not_4_out, not_3_out);
  and and_17 (and_17_out, not_3_out, in[2]);
  and and_18 (out[1], or_6_out, en);
  and and_19 (and_19_out, not_4_out, in[2]);
  or or_6 (or_6_out, and_19_out, in[3], and_17_out, and_16_out);
  and and_20 (and_20_out, in[1], not_2_out);
  and and_21 (and_21_out, not_3_out, in[2]);
  or or_7 (or_7_out, and_23_out, in[3], and_21_out, and_20_out);
  and and_22 (out[0], or_7_out, en);
  and and_23 (and_23_out, not_4_out, in[2]);
endmodule
