// Digital circuit io_module.dig as structural Verilog
module io_module (
  input  [9:0] num,
  input  [3:0] ops,
  input  eq,
  input  c,
  output [6:0] s1,
  output [6:0] s2,
  output [6:0] s3,
  output [6:0] s4,
  output [6:0] s5,
  output [6:0] s6,
  output [6:0] s7,
  output [6:0] s8,
  output a,
  output s,
  output m,
  output d,
  output err,
  output [6:0] r1,
  output [6:0] r2,
  output [6:0] r3,
  output [6:0] r4,
  output ne
);

  wire and_1_out, and_2_out, and_3_out, and_4_out, en1, en2, eno, or_1_out, r_n, u_en_2_out, u_en_3_out,
       u_flag_en_a, u_flag_en_b, u_number_inputs_enable;
  wire [3:0] u_flag_a, u_flag_b, u_number_inputs_out;
  wire [15:0] arithmetic_module_1_out, operand_storage_module_1_bin, operand_storage_module_2_bin,
       u_binary_to_bcd_out;

  number_inputs #(.applicationType("IVERILOG"), .CodeFile("C:\\Users\\metin\\Desktop\\Project101\\verilog_codes\\number_inputs.v")) u_number_inputs (
    .inp(num), .reset(r_n), .out(u_number_inputs_out), .enable(u_number_inputs_enable));
  operation_inputs #(.applicationType("IVERILOG"), .CodeFile("C:\\Users\\metin\\Desktop\\Project101\\verilog_codes\\operation_inputs.v")) u_operation_inputs (
    .inp(ops), .reset(c), .a(a), .s(s), .m(m), .d(d));
  or or_1 (or_1_out, d, m, s, a);
  or or_2 (r_n, c, or_1_out);
  en #(.applicationType("IVERILOG")) u_en (.res(c), .in(u_number_inputs_out), .out(en1));
  flag #(.applicationType("IVERILOG"), .CodeFile("C:\\Users\\metin\\Desktop\\Project101\\verilog_codes\\flag.v")) u_flag (
    .flag(or_1_out), .enable(u_number_inputs_enable), .number(u_number_inputs_out), .reset(c), .da(s4),
    .db(s8), .a(u_flag_a), .b(u_flag_b), .en_a(u_flag_en_a), .en_b(u_flag_en_b), .en2(en2));
  en #(.applicationType("IVERILOG")) u_en_2 (.en(u_flag_en_a), .res(c), .out(u_en_2_out));
  operand_storage_module operand_storage_module_1 (
    .num(u_flag_a), .en(u_en_2_out), .res(c), .ben(en1), .s1(s1), .s2(s2), .s3(s3), .s4(s4),
    .bin(operand_storage_module_1_bin));
  and and_1 (and_1_out, a, eq);
  and and_2 (and_2_out, s, eq);
  and and_3 (and_3_out, m, eq);
  and and_4 (and_4_out, d, eq);
  en #(.applicationType("IVERILOG")) u_en_3 (.en(u_flag_en_b), .res(c), .out(u_en_3_out));
  operand_storage_module operand_storage_module_2 (
    .num(u_flag_b), .en(u_en_3_out), .res(c), .ben(en2), .s1(s5), .s2(s6), .s3(s7), .s4(s8),
    .bin(operand_storage_module_2_bin));
  arithmetic_module arithmetic_module_1 (
    .in_a(operand_storage_module_1_bin), .in_b(operand_storage_module_2_bin), .a(and_1_out), .s(and_2_out),
    .m(and_3_out), .d(and_4_out), .c(c), .out(arithmetic_module_1_out), .err(err), .neg(ne), .en(eno));
  binary_to_bcd #(.applicationType("IVERILOG"), .CodeFile("C:\\Users\\metin\\Desktop\\Project101\\verilog_codes\\binary_to_bcd.v")) u_binary_to_bcd (
    .in(arithmetic_module_1_out), .out(u_binary_to_bcd_out));
  bcd_to_7s_encoder_module bcd_to_7s_encoder_module_1 (.in(u_binary_to_bcd_out[3:0]), .en(eno), .out(r1));
  bcd_to_7s_encoder_module bcd_to_7s_encoder_module_2 (.in(u_binary_to_bcd_out[7:4]), .en(eno), .out(r2));
  bcd_to_7s_encoder_module bcd_to_7s_encoder_module_3 (.in(u_binary_to_bcd_out[11:8]), .en(eno), .out(r3));
  bcd_to_7s_encoder_module bcd_to_7s_encoder_module_4 (.in(u_binary_to_bcd_out[15:12]), .en(eno), .out(r4));

  // Other names for the same wires on the sheet: diga[6:0] = s4; digb[6:0] = s8; res = c
endmodule

/* Code of en:
module en(
  input res,
  input [3:0] in,
  output reg out
);

  reg flag; // Flag to track the first change

  initial begin
    flag = 1'b0;
  end

  always @ (res) begin
    flag = 1'b0;
    out = 1'b0;
  end

  always @ (in) begin
    if (!flag && |in) begin
      flag = 1'b1;
      out = 1'b1;
    end else begin
      out = flag;
    end
  end

endmodule
*/

/* Code of en:
module en(
  input en,
  input res,
  output reg out
);

  always @(*) begin
    if (en || res) begin
      out = 1;
    end else begin
      out = 0;
    end
  end

endmodule
*/
