// Digital circuit operand_storage_module.dig as structural Verilog
module operand_storage_module (
  input  [3:0] num,
  input  en,
  input  res,
  input  ben,
  output [6:0] s1,
  output [6:0] s2,
  output [6:0] s3,
  output [6:0] s4,
  output [15:0] bin
);

  wire [3:0] d_ff_1_q, d_ff_2_q, d_ff_3_q, d_ff_4_q;
  wire [15:0] u_reset_3_o;

  D_FF #(.Bits(4)) d_ff_1 (.D(num), .C(en), .Q(d_ff_1_q));  // open: nQ
  reset #(.applicationType("IVERILOG"), .CodeFile("C:\\Users\\metin\\Desktop\\Project101\\verilog_codes\\reset.v")) u_reset (
    .r(res), .n(d_ff_1_q), .o(u_reset_3_o[3:0]));
  bcd_to_binary #(.applicationType("IVERILOG"), .CodeFile("C:\\Users\\metin\\Desktop\\Project101\\verilog_codes\\bcd_to_binary.v")) u_bcd_to_binary (
    .bcd_input(u_reset_3_o), .binary_output(bin));
  bcd_to_7s_encoder_module bcd_to_7s_encoder_module_1 (.in(u_reset_3_o[3:0]), .en(ben), .out(s1));
  D_FF #(.Bits(4)) d_ff_2 (.D(u_reset_3_o[3:0]), .C(en), .Q(d_ff_2_q));  // open: nQ
  reset #(.applicationType("IVERILOG"), .CodeFile("C:\\Users\\metin\\Desktop\\Project101\\verilog_codes\\reset.v")) u_reset_2 (
    .r(res), .n(d_ff_2_q), .o(u_reset_3_o[7:4]));
  bcd_to_7s_encoder_module bcd_to_7s_encoder_module_2 (.in(u_reset_3_o[7:4]), .en(ben), .out(s2));
  D_FF #(.Bits(4)) d_ff_3 (.D(u_reset_3_o[7:4]), .C(en), .Q(d_ff_3_q));  // open: nQ
  reset #(.applicationType("IVERILOG"), .CodeFile("C:\\Users\\metin\\Desktop\\Project101\\verilog_codes\\reset.v")) u_reset_3 (
    .r(res), .n(d_ff_3_q), .o(u_reset_3_o[11:8]));
  bcd_to_7s_encoder_module bcd_to_7s_encoder_module_3 (.in(u_reset_3_o[11:8]), .en(ben), .out(s3));
  D_FF #(.Bits(4)) d_ff_4 (.D(u_reset_3_o[11:8]), .C(en), .Q(d_ff_4_q));  // open: nQ
  reset #(.applicationType("IVERILOG"), .CodeFile("C:\\Users\\metin\\Desktop\\Project101\\verilog_codes\\reset.v")) u_reset_4 (
    .r(res), .n(d_ff_4_q), .o(u_reset_3_o[15:12]));
  bcd_to_7s_encoder_module bcd_to_7s_encoder_module_4 (.in(u_reset_3_o[15:12]), .en(ben), .out(s4));

  // Other names for the same wires on the sheet: en_t = ben
endmodule
